# Fritzing sketch prototype (saved by Fritzing 0.9.2b)
breadboards: 1

parts:
  Q1 = Basic FET N-Channel [package="TO220 [THT]"]
  L1 = Solenoid
  D1 = Rectifier Diode [part_number=1N4001 package="300 mil [THT]"]
  Bauteil1 = Arduino Uno (Rev3)
  Q2 = Basic FET N-Channel [package="TO220 [THT]"]
  D2 = Rectifier Diode [part_number=1N4001 package="300 mil [THT]"]
  L2 = Solenoid
  R1 = Resistor [tolerance=±5% resistance=680 package=THT]
  R2 = Resistor [tolerance=±5% resistance=680 package=THT]
  R3 = Resistor [tolerance=±5% resistance=10k package=THT]
  R4 = Resistor [tolerance=±5% resistance=10k package=THT]
  M1 = DC Motor
  Q3 = Basic FET N-Channel [package="TO220 [THT]"]
  R5 = Resistor [tolerance=±5% resistance=680 package=THT]
  R6 = Resistor [tolerance=±5% resistance=10k package=THT]
  D3 = Rectifier Diode [part_number=1N4001 package="300 mil [THT]"]

nets:
  N1: Q1.gate, R1.Pin_1
  N2: Q1.drain, L1.pin1, D1.anode
  N3: Q1.source, Bauteil1.GND, Q2.source, R3.Pin_0, R4.Pin_0, Q3.source, R6.Pin_0
  N4: L1.pin2, D1.cathode, Bauteil1.VIN, D2.cathode, L2.pin2, M1.pin_2, D3.cathode
  N5: Bauteil1.D2, R5.Pin_0, R6.Pin_1
  N6: Bauteil1.D3_PWM, R2.Pin_0, R4.Pin_1
  N7: Bauteil1.D4, R1.Pin_0, R3.Pin_1
  N8: Q2.gate, R2.Pin_1
  N9: Q2.drain, D2.anode, L2.pin1
  N10: M1.pin_1, Q3.drain, D3.anode
  N11: Q3.gate, R5.Pin_1
